# Fritzing sketch bytree (saved by Fritzing 0.9.1b)
breadboards: 1

parts:
  D1 = Rectifier Diode [part_number=1N4001 package="300 mil [THT]"]
  D2 = Rectifier Diode [part_number=1N4001 package="300 mil [THT]"]
  D3 = Rectifier Diode [part_number=1N4001 package="300 mil [THT]"]
  D4 = Rectifier Diode [part_number=1N4001 package="300 mil [THT]"]
  R1 = Resistor [tolerance=±5% resistance=22k package=THT]
  U1 = Optocoupler [package=THT]
  R2 = Resistor [tolerance=±5% resistance=10k package=THT]
  J1 = female pin header, 1 pin [form="♀ (female)"]
  J2 = female pin header, 1 pin [form="♀ (female)"]
  R3 = Resistor [tolerance=±5% resistance=1k package=THT]
  U2 = MOC3031-M [package=dil06]
  R4 = Resistor [tolerance=±5% resistance=470 package=THT]
  U3 = TRIAC [package=to-92]
  R5 = Resistor [tolerance=±5% resistance=1k package=THT]
  V3 = AC Power [voltage=127 frequency=60]
  V4 = AC Power [voltage=127 frequency=60]
  J3 = female pin header, 1 pin [form="♀ (female)"]
  J4 = female pin header, 1 pin [form="♀ (female)"]
  U4 = MOC3031-M [package=dil06]
  R6 = Resistor [tolerance=±5% resistance=470 package=THT]
  U5 = TRIAC [package=to-92]
  R7 = Resistor [tolerance=±5% resistance=1k package=THT]
  V5 = AC Power [voltage=127 frequency=60]

nets:
  N1: D1.cathode, D2.anode, V4.V+
  N2: D1.anode, D4.anode, U1.Pin_2
  N3: D2.cathode, D3.cathode, R1.Pin_0
  N4: D3.anode, D4.cathode, V4.V-
  N5: R1.Pin_1, U1.Pin_1
  GND: U1.Pin_4, R2.Pin_1, U2.2, U4.2
  P1.3: U1.Pin_5, R3.Pin_0
  N6: U1.Pin_6, R2.Pin_0
  N7: J1.pin1, R5.Pin_1, V3.V+
  N8: J2.pin1, U3.M2
  3.3V: R3.Pin_1
  N9: U2.1, R4.Pin_1
  N10: U2.4, U3.G
  N11: U2.6, R5.Pin_0
  P1.4: R4.Pin_0
  N12: U3.M1, V3.V-
  N13: J3.pin1, R7.Pin_1, V5.V+
  N14: J4.pin1, U5.M2
  N15: U4.1, R6.Pin_1
  N16: U4.4, U5.G
  N17: U4.6, R7.Pin_0
  P1.5: R6.Pin_0
  N18: U5.M1, V5.V-

notes:
  Detecçao de zero
  pisca-pisca
  Acionamento TRIAC
